// Logisim project 4_bit_adder.circ as structural Verilog: 2 circuits, main circuit full_adder_a9838687
module main (
  input  A0,
  input  A1,
  input  A2,
  input  A3,
  input  B0,
  input  B1,
  input  B2,
  input  B3,
  output Carry_out_1af93163,
  output S3,
  output S2,
  output S1,
  output S0
);

  wire dip_7408_1_p3, dip_7408_1_p4, dip_7408_1_p6, dip_7408_1_p9, dip_7408_1_p10, dip_7408_1_p11,
       dip_7408_1_p14, dip_7408_2_p4, dip_7408_2_p9, dip_7432_1_p6, dip_7432_1_p9, dip_7432_1_p10,
       dip_7432_1_p12, dip_7432_1_p13, dip_7432_1_p14;

  // DIP_7408 dip_7408_1: pin names not known; wires that end beside it: A0, B0, dip_7408_1_p3, dip_7408_1_p4, 1'b0, dip_7408_1_p6, 1'b0, 1'b1, dip_7408_1_p9, dip_7408_1_p10, dip_7408_1_p11, B1, A1, dip_7408_1_p14
  // DIP_7486 dip_7486_1: pin names not known; wires that end beside it: A0, B0, dip_7408_1_p4, dip_7408_1_p4, 1'b0, S0, 1'b0, 1'b1, dip_7408_1_p9, dip_7408_1_p10, S1, B1, A1, dip_7408_1_p10
  // DIP_7432 dip_7432_1: pin names not known; wires that end beside it: dip_7408_1_p3, dip_7408_1_p6, dip_7408_1_p9, dip_7408_1_p14, dip_7408_1_p11, dip_7432_1_p6, 1'b0, 1'b1, dip_7432_1_p9, dip_7432_1_p10, Carry_out_1af93163, dip_7432_1_p12, dip_7432_1_p13, dip_7432_1_p14
  // DIP_7408 dip_7408_2: pin names not known; wires that end beside it: A2, B2, dip_7432_1_p13, dip_7408_2_p4, dip_7432_1_p6, dip_7432_1_p12, 1'b1, dip_7432_1_p14, dip_7408_2_p9, dip_7432_1_p9, B3, A3
  // DIP_7486 dip_7486_2: pin names not known; wires that end beside it: 1'b0, A2, B2, dip_7408_2_p4, dip_7408_2_p4, dip_7432_1_p6, S2, 1'b0, dip_7432_1_p10, 1'b1, dip_7432_1_p14, dip_7408_2_p9, S3, B3, A3, dip_7408_2_p9

  // Notes on the sheet:
  //   4 bit adder with ripple carry
  //   AND
  //   XOR
  //   OR
  //   AND
  //   XOR
endmodule

module full_adder_a9838687 (
  input  bit_1,
  input  bit_2,
  input  Carry_in,
  output Sum,
  output Carry_out
);

  wire and_1_out, and_2_out, xor_1_out;

  xor xor_1 (xor_1_out, bit_1, bit_2);
  xor xor_2 (Sum, xor_1_out, Carry_in);
  and and_1 (and_1_out, Carry_in, xor_1_out);
  and and_2 (and_2_out, bit_1, bit_2);
  or or_1 (Carry_out, and_1_out, and_2_out);

  // Notes on the sheet:
  //   Full adder
endmodule
